# Fritzing sketch SWAGSKETBALL (saved by Fritzing 1.0.4)
breadboards: 1

parts:
  A1 = Particle - Photon2
  S1 = Pushbutton [package="[THT]"]
  R1 = Resistor [tolerance=±5% resistance=220 package="2512 [SMD]"]
  OLED_I2C1 = OLED 128x64 I2C Monochrome Display
  M1 = BMP280
  Q1 = LTR-301 [package=ltr-301]
  LD1 = LD
  R3 = Resistor [tolerance=±5% power=0.25W resistance=220 package=THT]
  S2 = Pushbutton [package="[THT]"]
  R4 = Resistor [tolerance=±5% resistance=220 package="2512 [SMD]"]
  R5 = Resistor [tolerance=±5% power=0.25W resistance=220 package=THT]

nets:
  N1: A1.Pin_4, A1.Pin_32, LD1.cathode, R3.Pin_0, R5.Pin_0
  N2: A1.Pin_7, S1.Pin_1, S1.Pin_2, R1.Pin_0
  N3: A1.Pin_8, LD1.anode, R5.Pin_1
  N4: A1.Pin_9, S2.Pin_1, S2.Pin_2, R4.Pin_0
  N5: A1.Pin_20, Q1.C
  VDD: A1.Pin_26, S1.Pin_3, S1.Pin_4, OLED_I2C1.VDD, M1.VIN, S2.Pin_3, S2.Pin_4
  GND: R1.Pin_1, OLED_I2C1.GND, M1.GND, R4.Pin_1
  N6: OLED_I2C1.SDA, M1.SDA
  N7: OLED_I2C1.SCK, M1.SCL
  N8: Q1.E, R3.Pin_1

custom parts:
  Particle - Photon2: The Photon 2 is a microcontroller and Wi-Fi networking developed by particle. Features: 802.11a/b/g/n Wi-Fi, 2.4 GHz and 5 GHz Integrated PCB antenna Integrated U.FL connector for external antenna Integrated RF switch BLE 5 using same antenna as Wi-Fi Realtek RTL8721DM MCU ARM Cortex M33 CPU, 200 MHz 2048 KB (2 MB) user application maximum size 3072 KB (3 MB) of RAM available to user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
  Pushbutton: A generic pushbutton.
  BMP280: Temperature Humidity Barometric presure Sensor, I2C
  LD: A Generic Red Dot Laser Diode Module (~5mW)
